# Fritzing sketch schematic (saved by Fritzing 0.9.3b)
breadboards: 1

parts:
  U1 = NodeMCU V3.0
  YL-83_-_Control_Board1 = YL-83 Rain Sensor - Control Board
  YL-83_-_Detection_Board1 = YL-83 Rain Sensor - Detection Board
  R1 = Resistor [tolerance=±5% resistance=220 package="0402 [SMD]"]
  R2 = PHOTOCELL [package=photocell]
  J1 = Basic Servo

nets:
  N1: U1.D4, J1.pulse
  3V3: U1.3V3, R2.P$1, J1.vcc
  N2: U1.GND#6, U1.GND#13, U1.GND#16, U1.GND#33, R1.Pin_0, J1.gnd
  N3: U1.A0, R1.Pin_1, R2.P$2
  N4: YL-83_-_Control_Board1.POS, YL-83_-_Detection_Board1.POS
  N5: YL-83_-_Control_Board1.NEG, YL-83_-_Detection_Board1.NEG

custom parts:
  NodeMCU V3.0: ESP8266 based NodeMCU
  YL-83 Rain Sensor - Control Board: The YL-83 is a rain sensor that has more resistance when dry and less resistance when wet. The module runs at 5V.
  YL-83 Rain Sensor - Detection Board: The YL-83 is a rain sensor that has more resistance when dry and less resistance when wet. The module runs at 5V.
